# Fritzing sketch voltmeter (saved by Fritzing 0.9.1b)
breadboards: 1

parts:
  R1 = Resistor [tolerance=±5% resistance=220 package=THT]
  R2 = Resistor [tolerance=±5% resistance=220 package=THT]
  Часть2 = Arduino Uno (Rev3)

nets:
  N1: R1.Pin_0, R2.Pin_0, Часть2.A1
  N2: R2.Pin_1, Часть2.GND

notes:
  R1 100кОм
  R2 10кОм
  Плюсовой щуп
  0--50В
